# Fritzing sketch ast_fritzing (saved by Fritzing 0.9.3b)
breadboards: 1

parts:
  Onderdeel1 = Photon
  Onderdeel2 = OLED Monochrome 128x64 0.96 inch [part_number=326]
  Onderdeel3 = Adafruit BME680
  IC1 = L293D [package=THT]
  U1 = RELAY-2 [package=relay-g5v]

nets:
  N1: Onderdeel1.A0, IC1.Enable_1
  N2: Onderdeel1.A1, IC1.In_1
  N3: Onderdeel1.A2, IC1.In_2
  GND: Onderdeel1.GND, Onderdeel2.GND, Onderdeel3.GND, IC1.0V
  VIN: Onderdeel1.VIN, Onderdeel2.VIN, IC1.+Vmotor, IC1.+V
  N4: Onderdeel1.D0, Onderdeel3.SDO/ADR
  N5: Onderdeel1.D1, Onderdeel3.SCK/SCL
  N6: Onderdeel1.D2, Onderdeel2.DC_SA0
  N7: Onderdeel1.D3, Onderdeel2.RESET
  N8: Onderdeel1.D4, Onderdeel2.CS
  N9: Onderdeel1.D5, Onderdeel2.MOSI_SDA
  N10: Onderdeel1.D6, Onderdeel2.SCLK_SCK
  3V3: Onderdeel1.3V3, Onderdeel3.3.3V
  N11: IC1.Out_1_(_Controlled_by_Enable_1_), U1.2
  N12: IC1.Out_2_(_Controlled_by_Enable_1_), U1.9

custom parts:
  OLED Monochrome 128x64 0.96 inch: These displays are small, only about 1" diameter, but very readable due to the high contrast of an OLED display. This display is made of 128x64 individual white OLED pixels, each one is turned on or off by the controller chip. Because the display makes its own light, no backlight is required. This reduces the power required to run the OLED and is why the display has such high contrast; we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
